# Fritzing sketch SmartGarden (saved by Fritzing 1.0.1rc)

parts:
  M1 = DOIT Esp32 DevKit v1 (30 pins long, 11 pins width) [part_number=ESP32S-PIN30]
  Part1 = FC-28 Soil Hygrometer Module
  Part2 = FC-28 Soil Hygrometer Module - Probe
  DS1 = DS18B20 1-Wire Temperature Sensor Probe
  M2 = water level switch
  Part3 = MQ-9 breakout
  J1 = Basic Servo
  J2 = Basic Servo
  M4 = DC Motor [voltage_(max)=6V voltage_(min)=3V]
  WATER_PUMP1 = water pump/motor
  Part4 = ACS712 Current Sensor 5A 20A 30A
  R1 = Photocell (LDR) [package=THT]
  R2 = Resistor [tolerance=±5% resistance=220 package="2010 [SMD]"]
  R3 = Photocell (LDR) [package=THT]
  R4 = Resistor [tolerance=±5% resistance=220 package="2010 [SMD]"]
  R5 = Photocell (LDR) [package=THT]
  R6 = Photocell (LDR) [package=THT]
  R7 = Resistor [tolerance=±5% resistance=220 package="2010 [SMD]"]
  R8 = Resistor [tolerance=±5% resistance=220 package="2010 [SMD]"]
  R9 = Resistor [tolerance=±5% resistance=4.7k package="2010 [SMD]"]
  R10 = Resistor [tolerance=±5% resistance=1k package="2010 [SMD]"]
  R11 = Resistor [tolerance=±5% resistance=2k package="2010 [SMD]"]
  Mod1 = Voltage Sensor 25V
  D1 = Diode [package=diode-1n4148]
  Q1 = PNP-Transistor [package="TO92 [THT]"]
  R13 = Resistor [tolerance=±5% resistance=220 package="2010 [SMD]"]
  D2 = Diode [package=diode-1n4148]
  Q2 = PNP-Transistor [package="TO92 [THT]"]
  R14 = Resistor [tolerance=±5% resistance=220 package="2010 [SMD]"]
  VCC1 = 4 x AAA Battery Mount
  Part5 = Solar Cell
  Part6 = KY-015 Temperature & Humidity Sensor Module [package="Breakout board"]

nets:
  3V3: M1.3V3, DS1.VDD, R1.pin_1, R3.pin_1, R5.pin_1, R6.pin_1
  GND: M1.GND, Part1.GND, DS1.GND, M2.pin2, Part3.GND, J1.gnd, J2.gnd, Part4.1, Part4.GND, R2.Pin_1, R4.Pin_1, R7.Pin_1, R8.Pin_1, R11.Pin_0, Mod1.GND, Mod1.-, Q1.C, Q2.C, VCC1.-, Part5.+, Part6.-
  N1: M1.D15, R1.pin_0, R2.Pin_0
  N2: M1.D2, R5.pin_0, R8.Pin_0
  N3: M1.D4, R3.pin_0, R4.Pin_0
  N4: M1.D5, R6.pin_0, R7.Pin_0
  N5: M1.D18, R9.Pin_1
  N6: M1.D19, M2.pin1
  N7: M1.D35, R14.Pin_1
  N8: M1.D32, R13.Pin_1
  N9: M1.D33, J2.pulse
  N10: M1.D25, J1.pulse
  N11: M1.D26, Part3.AO
  N12: M1.D27, Part6.S
  N13: M1.D14, Mod1.S
  N14: M1.D12, R10.Pin_1, R11.Pin_1
  N15: M1.D13, Part1.AO
  VCC: M1.VIN, Part1.VCC, Part3.VCC, J1.vcc, J2.vcc, M4.pin_2, WATER_PUMP1.pin_2, Part4.VCC, Mod1.+, D1.C, D2.C, VCC1.+, Part6.Vin
  N16: Part1.POS, Part2.POS
  N17: Part1.NEG, Part2.NEG
  N18: DS1.DQ, R9.Pin_0
  N19: WATER_PUMP1.pin_1, D2.A, Q2.E
  N20: Part4.2, Part4.OUT, R10.Pin_0, Mod1.VCC, Part5.-
  N21: D1.A, Q1.E
  N22: Q1.B, R13.Pin_0
  N23: Q2.B, R14.Pin_0

custom parts:
  DOIT Esp32 DevKit v1 (30 pins long, 11 pins width): The DOIT Esp32 DevKit v1 is one of the development board created by DOIT to evaluate the ESP-WROOM-32 module. It is based on the ESP32 microcontroller that boasts Wifi, Bluetooth, Ethernet and Low Power support all in a single chip. (vanepp) made breadboard work, adjusted pin numbering and labels and reduced size of schematic and cleaned up pcb. This chip is 30pins long (2 x15) and 11 pins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
  FC-28 Soil Hygrometer Module: The FC-28 is a soil hygrometer module that uses the Texas Instruments LM393 comparator chip to provide an analog measurement of soil humidity. The digital output is high when soil moisture is over a certain threshold, as determined by adjusting the potentiometer.
  FC-28 Soil Hygrometer Module - Probe: The FC-28 is a soil hygrometer module that uses the Texas Instruments LM393 comparator chip to provide an analog measurement of soil humidity.
  water level switch: Generic water level float switch.
  MQ-9 breakout: SKU: 101284
  water pump/motor: WATER PUMP BY ARDUBLOCKTR
  ACS712 Current Sensor 5A 20A 30A: Remix by Michael Kubina http://www.kubina.info Original by: https://forum.fritzing.org/t/current-sensor-5a-acs712/7694 https://forum.fritzing.org/u/ArtHome ArtHome12@gmail.com
  KY-015 Temperature & Humidity Sensor Module: KY-015 temperature and humidity sensor module, provides a low-latency serial interface to measure humidity and temperature.
